// Digital circuit Banc_de_Reg.dig as structural Verilog
module Banc_de_Reg (
  input  [31:0] Res,
  input  [4:0] Rd,
  input  W_Reg,
  input  [4:0] rs1,
  input  [4:0] rs2,
  output [31:0] SRC1,
  output [31:0] SRC2
);

  wire and_1_out, and_2_out, and_3_out, and_4_out, and_5_out, and_6_out, and_7_out, and_8_out, and_9_out,
       and_10_out, and_11_out, and_12_out, and_13_out, and_14_out, and_15_out, and_16_out, and_17_out,
       and_18_out, and_19_out, and_20_out, and_21_out, and_22_out, and_23_out, and_24_out, and_25_out,
       and_26_out, and_27_out, and_28_out, and_29_out, and_30_out, and_31_out, decoder_1_out_1,
       decoder_1_out_2, decoder_1_out_3, decoder_1_out_4, decoder_1_out_5, decoder_1_out_6, decoder_1_out_7,
       decoder_1_out_8, decoder_1_out_9, decoder_1_out_10, decoder_1_out_11, decoder_1_out_12,
       decoder_1_out_13, decoder_1_out_14, decoder_1_out_15, decoder_1_out_16, decoder_1_out_17,
       decoder_1_out_18, decoder_1_out_19, decoder_1_out_20, decoder_1_out_21, decoder_1_out_22,
       decoder_1_out_23, decoder_1_out_24, decoder_1_out_25, decoder_1_out_26, decoder_1_out_27,
       decoder_1_out_28, decoder_1_out_29, decoder_1_out_30, decoder_1_out_31, decoder_2_out_0,
       decoder_2_out_1, decoder_2_out_2, decoder_2_out_3, decoder_2_out_4, decoder_2_out_5, decoder_2_out_6,
       decoder_2_out_7, decoder_2_out_8, decoder_2_out_9, decoder_2_out_10, decoder_2_out_11,
       decoder_2_out_12, decoder_2_out_13, decoder_2_out_14, decoder_2_out_15, decoder_2_out_16,
       decoder_2_out_17, decoder_2_out_18, decoder_2_out_19, decoder_2_out_20, decoder_2_out_21,
       decoder_2_out_22, decoder_2_out_23, decoder_2_out_24, decoder_2_out_25, decoder_2_out_26,
       decoder_2_out_27, decoder_2_out_28, decoder_2_out_29, decoder_2_out_30, decoder_2_out_31,
       decoder_3_out_0, decoder_3_out_1, decoder_3_out_2, decoder_3_out_3, decoder_3_out_4, decoder_3_out_5,
       decoder_3_out_6, decoder_3_out_7, decoder_3_out_8, decoder_3_out_9, decoder_3_out_10,
       decoder_3_out_11, decoder_3_out_12, decoder_3_out_13, decoder_3_out_14, decoder_3_out_15,
       decoder_3_out_16, decoder_3_out_17, decoder_3_out_18, decoder_3_out_19, decoder_3_out_20,
       decoder_3_out_21, decoder_3_out_22, decoder_3_out_23, decoder_3_out_24, decoder_3_out_25,
       decoder_3_out_26, decoder_3_out_27, decoder_3_out_28, decoder_3_out_29, decoder_3_out_30,
       decoder_3_out_31;
  wire [31:0] R1_q, R2_q, R3_q, R4_q, R5_q, R6_q, R7_q, R8_q, R9_q, R10_q, R11_q, R12_q, R13_q, R14_q, R15_q,
       R16_q, R17_q, R18_q, R19_q, R20_q, R21_q, R22_q, R23_q, R24_q, R25_q, R26_q, R27_q, R28_q, R29_q,
       R30_q, R31_q;

  Decoder #(.Selector_Bits(5)) decoder_1 (
    .sel(Rd), .out_1(decoder_1_out_1), .out_2(decoder_1_out_2), .out_3(decoder_1_out_3),
    .out_4(decoder_1_out_4), .out_5(decoder_1_out_5), .out_6(decoder_1_out_6), .out_7(decoder_1_out_7),
    .out_8(decoder_1_out_8), .out_9(decoder_1_out_9), .out_10(decoder_1_out_10), .out_11(decoder_1_out_11),
    .out_12(decoder_1_out_12), .out_13(decoder_1_out_13), .out_14(decoder_1_out_14),
    .out_15(decoder_1_out_15), .out_16(decoder_1_out_16), .out_17(decoder_1_out_17),
    .out_18(decoder_1_out_18), .out_19(decoder_1_out_19), .out_20(decoder_1_out_20),
    .out_21(decoder_1_out_21), .out_22(decoder_1_out_22), .out_23(decoder_1_out_23),
    .out_24(decoder_1_out_24), .out_25(decoder_1_out_25), .out_26(decoder_1_out_26),
    .out_27(decoder_1_out_27), .out_28(decoder_1_out_28), .out_29(decoder_1_out_29),
    .out_30(decoder_1_out_30), .out_31(decoder_1_out_31));  // open: out_0
  and and_1 (and_1_out, W_Reg, decoder_1_out_1);
  and and_2 (and_2_out, W_Reg, decoder_1_out_2);
  and and_3 (and_3_out, W_Reg, decoder_1_out_3);
  and and_4 (and_4_out, W_Reg, decoder_1_out_4);
  and and_5 (and_5_out, W_Reg, decoder_1_out_5);
  and and_6 (and_6_out, W_Reg, decoder_1_out_6);
  and and_7 (and_7_out, W_Reg, decoder_1_out_7);
  and and_8 (and_8_out, W_Reg, decoder_1_out_8);
  and and_9 (and_9_out, W_Reg, decoder_1_out_9);
  and and_10 (and_10_out, W_Reg, decoder_1_out_10);
  and and_11 (and_11_out, W_Reg, decoder_1_out_11);
  and and_12 (and_12_out, W_Reg, decoder_1_out_12);
  and and_13 (and_13_out, W_Reg, decoder_1_out_13);
  and and_14 (and_14_out, W_Reg, decoder_1_out_14);
  and and_15 (and_15_out, W_Reg, decoder_1_out_15);
  and and_16 (and_16_out, W_Reg, decoder_1_out_16);
  and and_17 (and_17_out, W_Reg, decoder_1_out_17);
  and and_18 (and_18_out, W_Reg, decoder_1_out_18);
  and and_19 (and_19_out, W_Reg, decoder_1_out_19);
  and and_20 (and_20_out, W_Reg, decoder_1_out_20);
  and and_21 (and_21_out, W_Reg, decoder_1_out_21);
  and and_22 (and_22_out, W_Reg, decoder_1_out_22);
  and and_23 (and_23_out, W_Reg, decoder_1_out_23);
  and and_24 (and_24_out, W_Reg, decoder_1_out_24);
  and and_25 (and_25_out, W_Reg, decoder_1_out_25);
  and and_26 (and_26_out, W_Reg, decoder_1_out_26);
  and and_27 (and_27_out, W_Reg, decoder_1_out_27);
  and and_28 (and_28_out, W_Reg, decoder_1_out_28);
  and and_29 (and_29_out, W_Reg, decoder_1_out_29);
  and and_30 (and_30_out, W_Reg, decoder_1_out_30);
  and and_31 (and_31_out, W_Reg, decoder_1_out_31);
  D_FF #(.Bits(32)) R1 (.D(Res), .C(and_1_out), .Q(R1_q));  // open: nQ
  D_FF #(.Bits(32)) R2 (.D(Res), .C(and_2_out), .Q(R2_q));  // open: nQ
  D_FF #(.Bits(32)) R3 (.D(Res), .C(and_3_out), .Q(R3_q));  // open: nQ
  D_FF #(.Bits(32)) R4 (.D(Res), .C(and_4_out), .Q(R4_q));  // open: nQ
  D_FF #(.Bits(32)) R5 (.D(Res), .C(and_5_out), .Q(R5_q));  // open: nQ
  D_FF #(.Bits(32)) R6 (.D(Res), .C(and_6_out), .Q(R6_q));  // open: nQ
  D_FF #(.Bits(32)) R7 (.D(Res), .C(and_7_out), .Q(R7_q));  // open: nQ
  D_FF #(.Bits(32)) R8 (.D(Res), .C(and_8_out), .Q(R8_q));  // open: nQ
  D_FF #(.Bits(32)) R9 (.D(Res), .C(and_9_out), .Q(R9_q));  // open: nQ
  D_FF #(.Bits(32)) R10 (.D(Res), .C(and_10_out), .Q(R10_q));  // open: nQ
  D_FF #(.Bits(32)) R11 (.D(Res), .C(and_11_out), .Q(R11_q));  // open: nQ
  D_FF #(.Bits(32)) R12 (.D(Res), .C(and_12_out), .Q(R12_q));  // open: nQ
  D_FF #(.Bits(32)) R13 (.D(Res), .C(and_13_out), .Q(R13_q));  // open: nQ
  D_FF #(.Bits(32)) R14 (.D(Res), .C(and_14_out), .Q(R14_q));  // open: nQ
  D_FF #(.Bits(32)) R15 (.D(Res), .C(and_15_out), .Q(R15_q));  // open: nQ
  D_FF #(.Bits(32)) R16 (.D(Res), .C(and_16_out), .Q(R16_q));  // open: nQ
  D_FF #(.Bits(32)) R17 (.D(Res), .C(and_17_out), .Q(R17_q));  // open: nQ
  D_FF #(.Bits(32)) R18 (.D(Res), .C(and_18_out), .Q(R18_q));  // open: nQ
  D_FF #(.Bits(32)) R19 (.D(Res), .C(and_19_out), .Q(R19_q));  // open: nQ
  D_FF #(.Bits(32)) R20 (.D(Res), .C(and_20_out), .Q(R20_q));  // open: nQ
  D_FF #(.Bits(32)) R21 (.D(Res), .C(and_21_out), .Q(R21_q));  // open: nQ
  D_FF #(.Bits(32)) R22 (.D(Res), .C(and_22_out), .Q(R22_q));  // open: nQ
  D_FF #(.Bits(32)) R23 (.D(Res), .C(and_23_out), .Q(R23_q));  // open: nQ
  D_FF #(.Bits(32)) R24 (.D(Res), .C(and_24_out), .Q(R24_q));  // open: nQ
  D_FF #(.Bits(32)) R25 (.D(Res), .C(and_25_out), .Q(R25_q));  // open: nQ
  D_FF #(.Bits(32)) R26 (.D(Res), .C(and_26_out), .Q(R26_q));  // open: nQ
  D_FF #(.Bits(32)) R27 (.D(Res), .C(and_27_out), .Q(R27_q));  // open: nQ
  D_FF #(.Bits(32)) R28 (.D(Res), .C(and_28_out), .Q(R28_q));  // open: nQ
  D_FF #(.Bits(32)) R29 (.D(Res), .C(and_29_out), .Q(R29_q));  // open: nQ
  D_FF #(.Bits(32)) R30 (.D(Res), .C(and_30_out), .Q(R30_q));  // open: nQ
  D_FF #(.Bits(32)) R31 (.D(Res), .C(and_31_out), .Q(R31_q));  // open: nQ
  assign SRC1 = decoder_2_out_0 ? {32{1'b0}} : 32'bz;  // Driver driver_1
  assign SRC1 = decoder_2_out_1 ? R1_q : 32'bz;  // Driver driver_2
  assign SRC1 = decoder_2_out_2 ? R2_q : 32'bz;  // Driver driver_3
  assign SRC1 = decoder_2_out_3 ? R3_q : 32'bz;  // Driver driver_4
  assign SRC1 = decoder_2_out_4 ? R4_q : 32'bz;  // Driver driver_5
  assign SRC1 = decoder_2_out_5 ? R5_q : 32'bz;  // Driver driver_6
  assign SRC1 = decoder_2_out_6 ? R6_q : 32'bz;  // Driver driver_7
  assign SRC1 = decoder_2_out_7 ? R7_q : 32'bz;  // Driver driver_8
  assign SRC1 = decoder_2_out_8 ? R8_q : 32'bz;  // Driver driver_9
  assign SRC1 = decoder_2_out_9 ? R9_q : 32'bz;  // Driver driver_10
  Decoder #(.Selector_Bits(5)) decoder_2 (
    .sel(rs1), .out_0(decoder_2_out_0), .out_1(decoder_2_out_1), .out_2(decoder_2_out_2),
    .out_3(decoder_2_out_3), .out_4(decoder_2_out_4), .out_5(decoder_2_out_5), .out_6(decoder_2_out_6),
    .out_7(decoder_2_out_7), .out_8(decoder_2_out_8), .out_9(decoder_2_out_9), .out_10(decoder_2_out_10),
    .out_11(decoder_2_out_11), .out_12(decoder_2_out_12), .out_13(decoder_2_out_13),
    .out_14(decoder_2_out_14), .out_15(decoder_2_out_15), .out_16(decoder_2_out_16),
    .out_17(decoder_2_out_17), .out_18(decoder_2_out_18), .out_19(decoder_2_out_19),
    .out_20(decoder_2_out_20), .out_21(decoder_2_out_21), .out_22(decoder_2_out_22),
    .out_23(decoder_2_out_23), .out_24(decoder_2_out_24), .out_25(decoder_2_out_25),
    .out_26(decoder_2_out_26), .out_27(decoder_2_out_27), .out_28(decoder_2_out_28),
    .out_29(decoder_2_out_29), .out_30(decoder_2_out_30), .out_31(decoder_2_out_31));
  assign SRC1 = decoder_2_out_10 ? R10_q : 32'bz;  // Driver driver_11
  assign SRC1 = decoder_2_out_11 ? R11_q : 32'bz;  // Driver driver_12
  assign SRC1 = decoder_2_out_12 ? R12_q : 32'bz;  // Driver driver_13
  assign SRC1 = decoder_2_out_13 ? R13_q : 32'bz;  // Driver driver_14
  assign SRC1 = decoder_2_out_14 ? R14_q : 32'bz;  // Driver driver_15
  assign SRC1 = decoder_2_out_15 ? R15_q : 32'bz;  // Driver driver_16
  assign SRC1 = decoder_2_out_16 ? R16_q : 32'bz;  // Driver driver_17
  assign SRC1 = decoder_2_out_17 ? R17_q : 32'bz;  // Driver driver_18
  assign SRC1 = decoder_2_out_18 ? R18_q : 32'bz;  // Driver driver_19
  assign SRC1 = decoder_2_out_19 ? R19_q : 32'bz;  // Driver driver_20
  assign SRC1 = decoder_2_out_20 ? R20_q : 32'bz;  // Driver driver_21
  assign SRC1 = decoder_2_out_21 ? R21_q : 32'bz;  // Driver driver_22
  assign SRC1 = decoder_2_out_22 ? R22_q : 32'bz;  // Driver driver_23
  assign SRC1 = decoder_2_out_23 ? R23_q : 32'bz;  // Driver driver_24
  assign SRC1 = decoder_2_out_24 ? R24_q : 32'bz;  // Driver driver_25
  assign SRC1 = decoder_2_out_25 ? R25_q : 32'bz;  // Driver driver_26
  assign SRC1 = decoder_2_out_26 ? R26_q : 32'bz;  // Driver driver_27
  assign SRC1 = decoder_2_out_27 ? R27_q : 32'bz;  // Driver driver_28
  assign SRC1 = decoder_2_out_28 ? R28_q : 32'bz;  // Driver driver_29
  assign SRC1 = decoder_2_out_29 ? R29_q : 32'bz;  // Driver driver_30
  assign SRC1 = decoder_2_out_30 ? R30_q : 32'bz;  // Driver driver_31
  assign SRC1 = decoder_2_out_31 ? R31_q : 32'bz;  // Driver driver_32
  assign SRC2 = decoder_3_out_0 ? {32{1'b0}} : 32'bz;  // Driver driver_33
  assign SRC2 = decoder_3_out_1 ? R1_q : 32'bz;  // Driver driver_34
  assign SRC2 = decoder_3_out_2 ? R2_q : 32'bz;  // Driver driver_35
  assign SRC2 = decoder_3_out_3 ? R3_q : 32'bz;  // Driver driver_36
  assign SRC2 = decoder_3_out_4 ? R4_q : 32'bz;  // Driver driver_37
  assign SRC2 = decoder_3_out_5 ? R5_q : 32'bz;  // Driver driver_38
  assign SRC2 = decoder_3_out_6 ? R6_q : 32'bz;  // Driver driver_39
  assign SRC2 = decoder_3_out_7 ? R7_q : 32'bz;  // Driver driver_40
  assign SRC2 = decoder_3_out_8 ? R8_q : 32'bz;  // Driver driver_41
  assign SRC2 = decoder_3_out_9 ? R9_q : 32'bz;  // Driver driver_42
  assign SRC2 = decoder_3_out_10 ? R10_q : 32'bz;  // Driver driver_43
  Decoder #(.Selector_Bits(5)) decoder_3 (
    .sel(rs2), .out_0(decoder_3_out_0), .out_1(decoder_3_out_1), .out_2(decoder_3_out_2),
    .out_3(decoder_3_out_3), .out_4(decoder_3_out_4), .out_5(decoder_3_out_5), .out_6(decoder_3_out_6),
    .out_7(decoder_3_out_7), .out_8(decoder_3_out_8), .out_9(decoder_3_out_9), .out_10(decoder_3_out_10),
    .out_11(decoder_3_out_11), .out_12(decoder_3_out_12), .out_13(decoder_3_out_13),
    .out_14(decoder_3_out_14), .out_15(decoder_3_out_15), .out_16(decoder_3_out_16),
    .out_17(decoder_3_out_17), .out_18(decoder_3_out_18), .out_19(decoder_3_out_19),
    .out_20(decoder_3_out_20), .out_21(decoder_3_out_21), .out_22(decoder_3_out_22),
    .out_23(decoder_3_out_23), .out_24(decoder_3_out_24), .out_25(decoder_3_out_25),
    .out_26(decoder_3_out_26), .out_27(decoder_3_out_27), .out_28(decoder_3_out_28),
    .out_29(decoder_3_out_29), .out_30(decoder_3_out_30), .out_31(decoder_3_out_31));
  assign SRC2 = decoder_3_out_11 ? R11_q : 32'bz;  // Driver driver_44
  assign SRC2 = decoder_3_out_12 ? R12_q : 32'bz;  // Driver driver_45
  assign SRC2 = decoder_3_out_13 ? R13_q : 32'bz;  // Driver driver_46
  assign SRC2 = decoder_3_out_14 ? R14_q : 32'bz;  // Driver driver_47
  assign SRC2 = decoder_3_out_15 ? R15_q : 32'bz;  // Driver driver_48
  assign SRC2 = decoder_3_out_16 ? R16_q : 32'bz;  // Driver driver_49
  assign SRC2 = decoder_3_out_17 ? R17_q : 32'bz;  // Driver driver_50
  assign SRC2 = decoder_3_out_18 ? R18_q : 32'bz;  // Driver driver_51
  assign SRC2 = decoder_3_out_19 ? R19_q : 32'bz;  // Driver driver_52
  assign SRC2 = decoder_3_out_20 ? R20_q : 32'bz;  // Driver driver_53
  assign SRC2 = decoder_3_out_21 ? R21_q : 32'bz;  // Driver driver_54
  assign SRC2 = decoder_3_out_22 ? R22_q : 32'bz;  // Driver driver_55
  assign SRC2 = decoder_3_out_23 ? R23_q : 32'bz;  // Driver driver_56
  assign SRC2 = decoder_3_out_24 ? R24_q : 32'bz;  // Driver driver_57
  assign SRC2 = decoder_3_out_25 ? R25_q : 32'bz;  // Driver driver_58
  assign SRC2 = decoder_3_out_26 ? R26_q : 32'bz;  // Driver driver_59
  assign SRC2 = decoder_3_out_27 ? R27_q : 32'bz;  // Driver driver_60
  assign SRC2 = decoder_3_out_28 ? R28_q : 32'bz;  // Driver driver_61
  assign SRC2 = decoder_3_out_29 ? R29_q : 32'bz;  // Driver driver_62
  assign SRC2 = decoder_3_out_30 ? R30_q : 32'bz;  // Driver driver_63
  assign SRC2 = decoder_3_out_31 ? R31_q : 32'bz;  // Driver driver_64
endmodule
