// Digital circuit Branchement.dig as structural Verilog
module Branchement (
  input  [31:0] RES_UAL,
  input  [2:0] FCT3,
  input  On,
  output RES_Branch
);

  wire comparator_1_eq, comparator_1_lt, multiplexer_1_out, not_1_out, not_2_out;

  Comparator #(.Bits(32)) comparator_1 (
    .a(RES_UAL), .b({32{1'b0}}), .eq(comparator_1_eq), .lt(comparator_1_lt));  // open: gt
  not not_1 (not_1_out, comparator_1_eq);
  not not_2 (not_2_out, comparator_1_lt);
  Multiplexer #(.Selector_Bits(2)) multiplexer_1 (
    .sel({FCT3[2], FCT3[0]}), .in_0(comparator_1_eq), .in_1(not_1_out), .in_2(comparator_1_lt),
    .in_3(not_2_out), .out(multiplexer_1_out));
  and and_1 (RES_Branch, On, multiplexer_1_out);
endmodule
