// Digital circuit CIRCUIT_DE_CONTROLE_V1.dig as structural Verilog
module CIRCUIT_DE_CONTROLE_V1 (
  input  [6:0] OPCODE,
  input  [6:0] FCT7,
  input  CLK,
  output W_PC,
  output GATE_PC,
  output W_MAR,
  output OE,
  output WE,
  output W_MDR,
  output MUX_MDR,
  output GATE_MDR,
  output W_RI,
  output W_REG,
  output MUX_SW,
  output GATE_RS2,
  output MUX_ADD,
  output MUX_UAL,
  output GATE_UAL,
  output SUB,
  output BRANCH_ON,
  output JUMP_ON,
  output MUX_JALR
);

  wire and_1_out, and_2_out, and_3_out, and_4_out, and_5_out, and_6_out, and_7_out, and_8_out, and_9_out,
       and_10_out, and_11_out, and_12_out, and_13_out, and_14_out, and_15_out, and_16_out, decoder_1_out_0,
       decoder_1_out_1, decoder_1_out_2, decoder_1_out_3, decoder_1_out_4, decoder_1_out_5, decoder_1_out_7,
       decoder_1_out_8, decoder_1_out_11, decoder_1_out_12, decoder_1_out_13, decoder_1_out_17, or_1_out,
       or_2_out, or_3_out, or_4_out, or_5_out, or_6_out, or_7_out, or_8_out, or_9_out, or_10_out, or_11_out,
       or_12_out, or_13_out, or_14_out, or_15_out, or_16_out, or_17_out, or_18_out, or_19_out, or_20_out,
       or_21_out, or_22_out, or_23_out, or_24_out, or_27_out, or_28_out, or_29_out, or_33_out,
       select_opcode_1_b_type, select_opcode_1_i_type, select_opcode_1_jump_jal, select_opcode_1_jump_jalr,
       select_opcode_1_load, select_opcode_1_r_type, select_opcode_1_r_type__plus__sub, select_opcode_1_store;
  wire [4:0] D0_q;

  SELECT_OPCODE select_opcode_1 (
    .OPCODE(OPCODE), .FCT7(FCT7), .LOAD(select_opcode_1_load), .I_TYPE(select_opcode_1_i_type),
    .STORE(select_opcode_1_store), .R_TYPE__plus__SUB(select_opcode_1_r_type__plus__sub),
    .B_TYPE(select_opcode_1_b_type), .JUMP_JAL(select_opcode_1_jump_jal),
    .JUMP_JALR(select_opcode_1_jump_jalr), .R_TYPE(select_opcode_1_r_type));
  or or_1 (or_1_out, select_opcode_1_r_type__plus__sub, select_opcode_1_i_type, select_opcode_1_jump_jal, select_opcode_1_jump_jalr, select_opcode_1_load);
  or or_2 (or_2_out, select_opcode_1_r_type__plus__sub, select_opcode_1_b_type, select_opcode_1_jump_jal, select_opcode_1_jump_jalr, select_opcode_1_load, select_opcode_1_store);
  or or_3 (or_3_out, select_opcode_1_r_type, select_opcode_1_i_type, select_opcode_1_b_type, select_opcode_1_jump_jal, select_opcode_1_jump_jalr, select_opcode_1_store);
  or or_4 (or_4_out, select_opcode_1_load, select_opcode_1_store);
  or or_5 (or_5_out, select_opcode_1_jump_jal, select_opcode_1_jump_jalr);
  or or_6 (or_6_out, ~D0_q[1], ~D0_q[4]);  // Or
  or or_7 (or_7_out, ~D0_q[2], ~D0_q[4]);  // Or
  or or_8 (or_8_out, ~D0_q[3], ~D0_q[4]);  // Or
  or or_9 (or_9_out, ~D0_q[0], D0_q[1], D0_q[2]);  // Or
  or or_10 (or_10_out, D0_q[2], ~D0_q[3], select_opcode_1_jump_jal);  // Or
  or or_11 (or_11_out, ~D0_q[1], D0_q[2], ~D0_q[3]);  // Or
  or or_12 (or_12_out, ~D0_q[1], ~D0_q[2], D0_q[3]);  // Or
  or or_13 (or_13_out, D0_q[0], ~D0_q[1], D0_q[2], or_1_out);  // Or
  or or_14 (or_14_out, ~D0_q[0], ~D0_q[1], ~D0_q[3]);  // Or
  and and_1 (and_1_out, ~D0_q[4], ~D0_q[3], ~D0_q[2], ~D0_q[1], D0_q[0]);  // And
  and and_2 (and_2_out, or_2_out, ~D0_q[4], ~D0_q[3], ~D0_q[2], D0_q[1], ~D0_q[0]);  // And
  and and_3 (and_3_out, select_opcode_1_jump_jalr, ~D0_q[4], D0_q[3], ~D0_q[2], ~D0_q[1], ~D0_q[0]);  // And
  and and_4 (and_4_out, ~D0_q[4], D0_q[3], D0_q[2], D0_q[1], ~D0_q[0]);  // And
  and and_5 (and_5_out, or_3_out, ~D0_q[4], ~D0_q[3], ~D0_q[2], D0_q[1], ~D0_q[0]);  // And
  and and_6 (and_6_out, ~D0_q[4], D0_q[3], ~D0_q[2], D0_q[1], D0_q[0]);  // And
  and and_7 (and_7_out, ~D0_q[4], D0_q[3], D0_q[2], ~D0_q[1], ~D0_q[0]);  // And
  and and_8 (and_8_out, ~D0_q[4], D0_q[3], D0_q[2], D0_q[1], ~D0_q[0]);  // And
  and and_9 (and_9_out, or_4_out, ~D0_q[4], ~D0_q[3], ~D0_q[2], D0_q[1], ~D0_q[0]);  // And
  and and_10 (and_10_out, ~D0_q[4], ~D0_q[3], D0_q[2], D0_q[1], D0_q[0]);  // And
  and and_11 (and_11_out, or_5_out, ~D0_q[4], D0_q[3], ~D0_q[2], ~D0_q[1], ~D0_q[0]);  // And
  and and_12 (and_12_out, ~D0_q[4], D0_q[3], ~D0_q[2], D0_q[1], D0_q[0]);  // And
  and and_13 (and_13_out, ~D0_q[4], D0_q[3], D0_q[2], ~D0_q[1], ~D0_q[0]);  // And
  and and_14 (and_14_out, ~D0_q[4], D0_q[3], D0_q[2], D0_q[1], ~D0_q[0]);  // And
  or or_15 (or_15_out, D0_q[0], ~D0_q[1]);  // Or
  or or_16 (or_16_out, D0_q[0], ~D0_q[3]);  // Or
  or or_17 (or_17_out, D0_q[2], ~D0_q[3]);  // Or
  or or_18 (or_18_out, ~D0_q[0], ~D0_q[4]);  // Or
  or or_19 (or_19_out, ~D0_q[2], ~D0_q[4]);  // Or
  or or_20 (or_20_out, D0_q[1], D0_q[2], D0_q[4]);
  or or_21 (or_21_out, ~D0_q[1], ~D0_q[2], D0_q[3]);  // Or
  and and_15 (and_15_out, or_6_out, or_7_out, or_8_out, or_9_out, or_10_out, or_11_out, or_12_out, or_13_out, or_14_out);
  or or_22 (or_22_out, and_1_out, and_2_out, and_3_out, and_4_out);
  or or_23 (or_23_out, and_5_out, and_6_out, and_7_out, and_8_out);
  or or_24 (or_24_out, and_9_out, and_10_out, and_11_out, and_12_out, and_13_out, and_14_out);
  and and_16 (and_16_out, or_15_out, or_16_out, or_17_out, or_18_out, or_19_out, or_20_out, or_21_out);
  D_FF D0 (.D(and_15_out), .C(CLK), .Q(D0_q[0]));  // open: nQ
  D_FF D1 (.D(or_22_out), .C(CLK), .Q(D0_q[1]));  // open: nQ
  D_FF D2 (.D(or_23_out), .C(CLK), .Q(D0_q[2]));  // open: nQ
  D_FF D3 (.D(or_24_out), .C(CLK), .Q(D0_q[3]));  // open: nQ
  D_FF D4 (.D(and_16_out), .C(CLK), .Q(D0_q[4]));  // open: nQ
  Decoder #(.Selector_Bits(5)) decoder_1 (
    .sel(D0_q), .out_0(decoder_1_out_0), .out_1(decoder_1_out_1), .out_2(decoder_1_out_2),
    .out_3(decoder_1_out_3), .out_4(decoder_1_out_4), .out_5(decoder_1_out_5), .out_6(BRANCH_ON),
    .out_7(decoder_1_out_7), .out_8(decoder_1_out_8), .out_9(JUMP_ON), .out_10(MUX_JALR),
    .out_11(decoder_1_out_11), .out_12(decoder_1_out_12), .out_13(decoder_1_out_13), .out_14(MUX_SW),
    .out_15(GATE_RS2), .out_16(OE), .out_17(decoder_1_out_17));  // open: out_18, out_19, out_20, out_21, out_22, out_23, out_24, out_25, out_26, out_27, out_28, out_29, out_30, out_31
  or or_25 (GATE_PC, decoder_1_out_0, decoder_1_out_8);
  or or_26 (MUX_MDR, decoder_1_out_1, decoder_1_out_12);
  or or_27 (or_27_out, BRANCH_ON, decoder_1_out_7, JUMP_ON, MUX_JALR, decoder_1_out_17);
  or or_28 (or_28_out, decoder_1_out_0, decoder_1_out_11, MUX_SW);
  Delay #(.delayTime(5)) delay_1 (.in(or_28_out), .out(W_MAR));
  or or_29 (or_29_out, decoder_1_out_1, decoder_1_out_12, GATE_RS2);
  or or_30 (MUX_ADD, MUX_JALR, decoder_1_out_11, MUX_SW);
  or or_31 (MUX_UAL, decoder_1_out_5, MUX_JALR, decoder_1_out_11, MUX_SW);
  or or_32 (SUB, decoder_1_out_3, BRANCH_ON);
  Delay #(.delayTime(6)) delay_2 (.in(or_27_out), .out(W_PC));
  Delay #(.delayTime(7)) delay_3 (.in(or_29_out), .out(W_MDR));
  or or_33 (or_33_out, decoder_1_out_4, decoder_1_out_5, decoder_1_out_3, decoder_1_out_8, decoder_1_out_13);
  or or_34 (GATE_UAL, decoder_1_out_4, decoder_1_out_5, MUX_JALR, decoder_1_out_11, MUX_SW, decoder_1_out_3);
  Delay #(.delayTime(5)) delay_4 (.in(or_33_out), .out(W_REG));
  or or_35 (GATE_MDR, decoder_1_out_2, JUMP_ON, decoder_1_out_13);
  Delay #(.delayTime(5)) delay_5 (.in(decoder_1_out_2), .out(W_RI));

  assign WE = OE;
endmodule
