// Digital circuit ProcesseurV1CC.dig as structural Verilog
module ProcesseurV1CC (
  input  clk,
  output [31:0] RES
);

  wire circuit_de_controle_v1_1_branch_on, circuit_de_controle_v1_1_gate_mdr,
       circuit_de_controle_v1_1_gate_pc, circuit_de_controle_v1_1_gate_rs2,
       circuit_de_controle_v1_1_gate_ual, circuit_de_controle_v1_1_mux_add,
       circuit_de_controle_v1_1_mux_jalr, circuit_de_controle_v1_1_mux_mdr, circuit_de_controle_v1_1_mux_sw,
       circuit_de_controle_v1_1_mux_ual, circuit_de_controle_v1_1_oe, circuit_de_controle_v1_1_sub,
       circuit_de_controle_v1_1_w_mar, circuit_de_controle_v1_1_w_mdr, circuit_de_controle_v1_1_w_pc,
       circuit_de_controle_v1_1_w_reg, circuit_de_controle_v1_1_w_ri, circuit_de_controle_v1_1_we, not_1_out;
  wire [1:0] branchement_1_res_branch;
  wire [2:0] multiplexer_6_out, RI_q_4;
  wire [3:0] RI_q_3;
  wire [6:0] RI_q, RI_q_5;
  wire [7:0] MAR_q;
  wire [11:0] multiplexer_3_out;
  wire [24:7] RI_q_2;
  wire [31:0] banc_de_reg_1_src1, banc_de_reg_1_src2, bitextender_1_out, bitextender_2_out,
       bitextender_3_out, driver_3_out, MDR_q, multiplexer_1_out, multiplexer_2_out, multiplexer_4_out,
       multiplexer_5_out, PC_q, plus_s, ual_1_s;

  Multiplexer #(.Selector_Bits(2), .Bits(32)) multiplexer_1 (
    .sel(branchement_1_res_branch), .in_0(32'h4), .in_1(bitextender_2_out), .in_2(bitextender_1_out),
    .in_3({32{1'b0}}), .out(multiplexer_1_out));
  BitExtender #(.inputBits(21), .outputBits(32)) bitextender_1 (
    .in({RES[31], RES[19:12], RES[20], RES[30:21], 1'b0}), .out(bitextender_1_out));
  Add #(.Bits(32)) plus (.a(PC_q), .b(multiplexer_1_out), .c_i(1'b0), .s(plus_s));  // open: c_o
  BitExtender #(.inputBits(13), .outputBits(32)) bitextender_2 (
    .in({RI_q_5[6], RI_q_2[7], RI_q_5[5:0], RI_q_3, 1'b0}), .out(bitextender_2_out));
  Multiplexer #(.Bits(32)) multiplexer_2 (
    .sel(circuit_de_controle_v1_1_mux_jalr), .in_0(plus_s), .in_1(RES), .out(multiplexer_2_out));
  D_FF #(.Bits(32)) PC (.D(multiplexer_2_out), .C(circuit_de_controle_v1_1_w_pc), .Q(PC_q));  // open: nQ
  assign RES = circuit_de_controle_v1_1_gate_pc ? PC_q : 32'bz;  // Driver driver_1
  CIRCUIT_DE_CONTROLE_V1 circuit_de_controle_v1_1 (
    .OPCODE(RI_q), .FCT7(RI_q_5), .CLK(clk), .W_PC(circuit_de_controle_v1_1_w_pc),
    .GATE_PC(circuit_de_controle_v1_1_gate_pc), .W_MAR(circuit_de_controle_v1_1_w_mar),
    .OE(circuit_de_controle_v1_1_oe), .WE(circuit_de_controle_v1_1_we),
    .W_MDR(circuit_de_controle_v1_1_w_mdr), .MUX_MDR(circuit_de_controle_v1_1_mux_mdr),
    .GATE_MDR(circuit_de_controle_v1_1_gate_mdr), .W_RI(circuit_de_controle_v1_1_w_ri),
    .W_REG(circuit_de_controle_v1_1_w_reg), .MUX_SW(circuit_de_controle_v1_1_mux_sw),
    .GATE_RS2(circuit_de_controle_v1_1_gate_rs2), .MUX_ADD(circuit_de_controle_v1_1_mux_add),
    .MUX_UAL(circuit_de_controle_v1_1_mux_ual), .GATE_UAL(circuit_de_controle_v1_1_gate_ual),
    .SUB(circuit_de_controle_v1_1_sub), .BRANCH_ON(circuit_de_controle_v1_1_branch_on),
    .JUMP_ON(branchement_1_res_branch[1]), .MUX_JALR(circuit_de_controle_v1_1_mux_jalr));
  Branchement branchement_1 (
    .RES_UAL(ual_1_s), .FCT3(RI_q_4), .On(circuit_de_controle_v1_1_branch_on),
    .RES_Branch(branchement_1_res_branch[0]));
  D_FF #(.Bits(32)) RI (
    .D(RES), .C(circuit_de_controle_v1_1_w_ri), .Q({RI_q_5, RI_q_2[24:15], RI_q_4, RI_q_3, RI_q_2[7], RI_q}));  // open: nQ
  D_FF #(.Bits(8)) MAR (.D(RES[9:2]), .C(circuit_de_controle_v1_1_w_mar), .Q(MAR_q));  // open: nQ
  Multiplexer #(.Bits(12)) multiplexer_3 (
    .sel(circuit_de_controle_v1_1_mux_sw), .in_0({RI_q_5, RI_q_2[24:20]}),
    .in_1({RI_q_5, RI_q_3, RI_q_2[7]}), .out(multiplexer_3_out));
  Multiplexer #(.Bits(32)) multiplexer_4 (
    .sel(circuit_de_controle_v1_1_mux_mdr), .in_0(RES), .in_1(driver_3_out), .out(multiplexer_4_out));
  D_FF #(.Bits(32)) MDR (.D(multiplexer_4_out), .C(circuit_de_controle_v1_1_w_mdr), .Q(MDR_q));  // open: nQ
  Banc_de_Reg banc_de_reg_1 (
    .Res(RES), .Rd({RI_q_3, RI_q_2[7]}), .W_Reg(circuit_de_controle_v1_1_w_reg), .rs1(RI_q_2[19:15]),
    .rs2(RI_q_2[24:20]), .SRC1(banc_de_reg_1_src1), .SRC2(banc_de_reg_1_src2));
  assign RES = circuit_de_controle_v1_1_gate_mdr ? MDR_q : 32'bz;  // Driver driver_2
  assign driver_3_out = circuit_de_controle_v1_1_oe ? MDR_q : 32'bz;  // Driver driver_3
  BitExtender #(.inputBits(12), .outputBits(32)) bitextender_3 (.in(multiplexer_3_out), .out(bitextender_3_out));
  assign RES = circuit_de_controle_v1_1_gate_rs2 ? banc_de_reg_1_src2 : 32'bz;  // Driver driver_4
  Multiplexer #(.Bits(32)) multiplexer_5 (
    .sel(circuit_de_controle_v1_1_mux_ual), .in_0(banc_de_reg_1_src2), .in_1(bitextender_3_out),
    .out(multiplexer_5_out));
  Multiplexer #(.Bits(3)) multiplexer_6 (
    .sel(circuit_de_controle_v1_1_mux_add), .in_0(RI_q_4), .in_1(3'b000), .out(multiplexer_6_out));
  not not_1 (not_1_out, circuit_de_controle_v1_1_oe);
  RAMSinglePortSel #(.AddrBits(8), .Bits(32)) ramsingleportsel_1 (
    .A(MAR_q), .CS(1'b1), .WE(circuit_de_controle_v1_1_we), .OE(not_1_out), .D(driver_3_out));
  UAL ual_1 (
    .FCT7_5(circuit_de_controle_v1_1_sub), .A(banc_de_reg_1_src1), .B(multiplexer_5_out),
    .FCT3(multiplexer_6_out), .S(ual_1_s));  // open: Cout
  assign RES = circuit_de_controle_v1_1_gate_ual ? ual_1_s : 32'bz;  // Driver driver_5
endmodule
