// Digital circuit SELECT_OPCODE.dig as structural Verilog
module SELECT_OPCODE (
  input  [6:0] OPCODE,
  input  [6:0] FCT7,
  output LOAD,
  output I_TYPE,
  output STORE,
  output R_TYPE__plus__SUB,
  output B_TYPE,
  output JUMP_JAL,
  output JUMP_JALR,
  output R_TYPE
);

  wire decoder_1_out_12;

  Decoder #(.Selector_Bits(5)) decoder_1 (
    .sel(OPCODE[6:2]), .out_0(LOAD), .out_4(I_TYPE), .out_8(STORE), .out_12(decoder_1_out_12),
    .out_24(B_TYPE), .out_25(JUMP_JALR), .out_27(JUMP_JAL));  // open: out_1, out_2, out_3, out_5, out_6, out_7, out_9, out_10, out_11, out_13, out_14, out_15, out_16, out_17, out_18, out_19, out_20, out_21, out_22, out_23, out_26, out_28, out_29, out_30, out_31
  and and_1 (R_TYPE__plus__SUB, decoder_1_out_12, FCT7[5]);
  and and_2 (R_TYPE, decoder_1_out_12, ~FCT7[5]);  // And
endmodule
